# Fritzing sketch wiring (saved by Fritzing 0.9.3b)
breadboards: 1

parts:
  Part1 = Arduino Uno (Rev3)
  S1 = Pushbutton [package="[THT]"]

nets:
  N1: Part1.D8, Part1.GND, S1.Pin_1, S1.Pin_2
  N2: Part1.D10_PWM/SS, S1.Pin_3, S1.Pin_4

notes:
  spin button
